# Fritzing sketch iot_vt (saved by Fritzing 0.9.4)
breadboards: 1

parts:
  Part1 = Arduino Nano 33 IOT
  Q1 = NPN-Transistor [package="TO92 [THT]"]
  R1 = Resistor [tolerance=±5% resistance=220 package="2010 [SMD]"]
  R2 = Resistor [tolerance=±5% resistance=220 package="2010 [SMD]"]
  U1 = Vibration Motor- ROB-08449 [package=vibe-motor-10mm]

nets:
  N1: Part1.RESET, Part1.A7
  N2: Part1.GND, Part1.D13~, R1.Pin_0
  N3: Part1.D2, R2.Pin_0
  N4: Part1.D11/MOSI, Part1.+5V
  N5: Part1.3V3, U1.-
  N6: Q1.E, R1.Pin_1
  N7: Q1.B, U1.+
  N8: Q1.C, R2.Pin_1

custom parts:
  Arduino Nano 33 IOT: The Arduino Nano 33 IoT is the easiest and cheapest point of entry to enhance existing devices (and creating new ones) to be part of the IoT and designing pico-network applications. Whether you are looking at building a sensor network connected to your office or home router, or if you want to create a BLE device sending data to a cellphone, the Nano 33 IoT is your one-stop-solution for many of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
